// Logisim project ex2.circ as structural Verilog: 1 circuit, main circuit compute_BrUn
module compute_BrUn (
  input  [31:0] INSTRUCTION,
  output BrUn
);

  wire [6:0] and_1_out;

  assign and_1_out = 7'b1100011 & INSTRUCTION[6:0];  // AND_Gate and_1, 7 bits wide
  Multiplexer #(.enable("true"), .select(3)) multiplexer_1 (
    .in0(1'b0), .in1(1'b0), .in2(1'b0), .in3(1'b0), .in4(1'b0), .in5(1'b0), .in6(1'b1), .in7(1'b1),
    .out(BrUn), .sel(INSTRUCTION[14:12]), .en(and_1_out[0]));
endmodule
