// Logisim project control-logic.circ as structural Verilog: 1 circuit, main circuit control_logic
module control_logic (
  input  [31:0] Instruction,
  input  BrEq,
  input  BrLt,
  output PCSel,
  output RegWEn,
  output [2:0] ImmSel,
  output BrUn,
  output ASel,
  output BSel,
  output [3:0] ALUSel,
  output MemWEn,
  output [1:0] WBSel
);

  wire B_type, funct3_000, funct3_001, funct3_010, funct3_011, funct3_100, funct3_101, funct3_110,
       funct3_111, funct7_0000000, funct7_0000001, funct7_0100000, I_type_1, I_type_2, is_add, is_addi,
       is_and, is_andi, is_auipc, is_beq, is_bge, is_bgeu, is_blt, is_bltu, is_bne, is_jal, is_jalr, is_lb,
       is_lh, is_lui, is_lw, is_mul, is_mulh, is_mulhu, is_or, is_ori, is_sb, is_sh, is_sll, is_slli, is_slt,
       is_slti, is_sra, is_srai, is_srl, is_srli, is_sub, is_sw, is_xor, is_xori, not_1_out, not_2_out,
       or_1_out, R_type, S_type;
  wire [2:0] branch_index;
  wire [5:0] ROM_index;
  wire [15:14] rom_1_data;

  ROM #(.addrWidth(6), .dataWidth(16)) rom_1 (
    .addr(ROM_index), .data({rom_1_data, WBSel, MemWEn, ALUSel, BSel, ASel, BrUn, ImmSel, RegWEn}));
  Comparator #(.width(7)) comparator_1 (.a(Instruction[6:0]), .b(7'b0110011), .eq(R_type));  // open: gt, lt
  Comparator #(.width(7)) comparator_2 (.a(Instruction[6:0]), .b(7'b0000011), .eq(I_type_1));  // open: gt, lt
  Comparator #(.width(7)) comparator_3 (.a(Instruction[6:0]), .b(7'b0010011), .eq(I_type_2));  // open: gt, lt
  Comparator #(.width(7)) comparator_4 (.a(Instruction[6:0]), .b(7'b0100011), .eq(S_type));  // open: gt, lt
  Comparator #(.width(7)) comparator_5 (.a(Instruction[6:0]), .b(7'b1100011), .eq(B_type));  // open: gt, lt
  Comparator #(.width(7)) comparator_6 (.a(Instruction[6:0]), .b(7'b0010111), .eq(is_auipc));  // open: gt, lt
  Comparator #(.width(7)) comparator_7 (.a(Instruction[6:0]), .b(7'b0110111), .eq(is_lui));  // open: gt, lt
  Comparator #(.width(7)) comparator_8 (.a(Instruction[6:0]), .b(7'b1101111), .eq(is_jal));  // open: gt, lt
  Comparator #(.width(7)) comparator_9 (.a(Instruction[6:0]), .b(7'b1100111), .eq(is_jalr));  // open: gt, lt
  Priority_Encoder #(.select_enc(6)) priority_encoder_1 (
    .in0(is_add), .in1(is_mul), .in2(is_sub), .in3(is_sll), .in4(is_mulh), .in5(is_mulhu), .in6(is_slt),
    .in7(is_xor), .in8(is_srl), .in9(is_sra), .in10(is_or), .in11(is_and), .in12(is_lb), .in13(is_lh),
    .in14(is_lw), .in15(is_addi), .in16(is_slli), .in17(is_slti), .in18(is_xori), .in19(is_srli),
    .in20(is_srai), .in21(is_ori), .in22(is_andi), .in23(is_sb), .in24(is_sh), .in25(is_sw), .in26(is_beq),
    .in27(is_bne), .in28(is_blt), .in29(is_bge), .in30(is_bltu), .in31(is_bgeu), .in32(is_auipc),
    .in33(is_lui), .in34(is_jal), .in35(is_jalr), .out(ROM_index));  // open: in36, in37, in38, in39, in40, in41, in42, in43, in44, in45, in46, in47, in48, in49, in50, in51, in52, in53, in54, in55, in56, in57, in58, in59, in60, in61, in62, in63, gs, en_out, en_in
  Comparator #(.width(3)) comparator_10 (.a(Instruction[14:12]), .b(3'b000), .eq(funct3_000));  // open: gt, lt
  Comparator #(.width(3)) comparator_11 (.a(Instruction[14:12]), .b(3'b001), .eq(funct3_001));  // open: gt, lt
  Comparator #(.width(3)) comparator_12 (.a(Instruction[14:12]), .b(3'b010), .eq(funct3_010));  // open: gt, lt
  Comparator #(.width(3)) comparator_13 (.a(Instruction[14:12]), .b(3'b011), .eq(funct3_011));  // open: gt, lt
  Comparator #(.width(3)) comparator_14 (.a(Instruction[14:12]), .b(3'b100), .eq(funct3_100));  // open: gt, lt
  Comparator #(.width(3)) comparator_15 (.a(Instruction[14:12]), .b(3'b101), .eq(funct3_101));  // open: gt, lt
  Comparator #(.width(3)) comparator_16 (.a(Instruction[14:12]), .b(3'b110), .eq(funct3_110));  // open: gt, lt
  Comparator #(.width(3)) comparator_17 (.a(Instruction[14:12]), .b(3'b111), .eq(funct3_111));  // open: gt, lt
  Comparator #(.width(7)) comparator_18 (.a(Instruction[31:25]), .b({7{1'b0}}), .eq(funct7_0000000));  // open: gt, lt
  Comparator #(.width(7)) comparator_19 (.a(Instruction[31:25]), .b(7'b0000001), .eq(funct7_0000001));  // open: gt, lt
  Comparator #(.width(7)) comparator_20 (.a(Instruction[31:25]), .b(7'b0100000), .eq(funct7_0100000));  // open: gt, lt
  Multiplexer #(.select(3)) multiplexer_1 (
    .in0(1'b0), .in1(BrEq), .in2(not_1_out), .in3(BrLt), .in4(not_2_out), .in5(BrLt), .in6(not_2_out),
    .in7(1'b1), .out(PCSel), .sel(branch_index));
  or or_1 (or_1_out, is_jal, is_jalr);
  Priority_Encoder priority_encoder_2 (
    .in0(1'b1), .in1(is_beq), .in2(is_bne), .in3(is_blt), .in4(is_bge), .in5(is_bltu), .in6(is_bgeu),
    .in7(or_1_out), .out(branch_index));  // open: en_in, gs, en_out
  not not_1 (not_1_out, BrEq);
  not not_2 (not_2_out, BrLt);
  and and_1 (is_addi, I_type_2, funct3_000);
  and and_2 (is_slli, I_type_2, funct3_001);
  and and_3 (is_slti, I_type_2, funct3_010);
  and and_4 (is_xori, I_type_2, funct3_100);
  and and_5 (is_ori, I_type_2, funct3_110);
  and and_6 (is_andi, I_type_2, funct3_111);
  and and_7 (is_beq, B_type, funct3_000);
  and and_8 (is_bne, B_type, funct3_001);
  and and_9 (is_blt, B_type, funct3_100);
  and and_10 (is_bge, B_type, funct3_101);
  and and_11 (is_bltu, B_type, funct3_110);
  and and_12 (is_bgeu, B_type, funct3_111);
  and and_13 (is_sb, S_type, funct3_000);
  and and_14 (is_sh, S_type, funct3_001);
  and and_15 (is_sw, S_type, funct3_010);
  and and_16 (is_add, R_type, funct3_000, funct7_0000000);
  and and_17 (is_mul, R_type, funct3_000, funct7_0000001);
  and and_18 (is_sub, R_type, funct3_000, funct7_0100000);
  and and_19 (is_sll, R_type, funct3_001, funct7_0000000);
  and and_20 (is_mulh, R_type, funct3_001, funct7_0000001);
  and and_21 (is_mulhu, R_type, funct3_011);
  and and_22 (is_slt, R_type, funct3_010);
  and and_23 (is_xor, R_type, funct3_100);
  and and_24 (is_srl, R_type, funct3_101, funct7_0000000);
  and and_25 (is_sra, R_type, funct3_101, funct7_0100000);
  and and_26 (is_or, R_type, funct3_110);
  and and_27 (is_and, R_type, funct3_111);
  and and_28 (is_lb, I_type_1, funct3_000);
  and and_29 (is_lh, I_type_1, funct3_001);
  and and_30 (is_lw, I_type_1, funct3_010);
  and and_31 (is_srli, I_type_2, funct3_101, funct7_0000000);
  and and_32 (is_srai, I_type_2, funct3_101, funct7_0100000);

  // Notes on the sheet:
  //   INPUTS to your circuit
  //   contents of rom_1 (hex, n*v repeats v):
  //   1001 1401 1601 1081 1481 1581 1101 1201 1281 1681 1301 1381 41 41 41 1041 10c1 1141 1241 12c1 16c1
  //   1341 13c1 842 842 842 4*64 74 74 1067 17c7 2069 2041
  //   ROM FOR CONTROL LOGIC
  //   DON'T CHANGE THE LOCATIONS OF THE INPUTS AND OUTPUTS!
  //   This is only if you choose to do the ROM option
  //   CONNECT
  //   WIRE
  //   TO
  //   USE
  //   ROM
  //   OUTPUT from your circuit
  //   Reminder: If using ROM, use combinational logic for PCSel
endmodule
