// Logisim project partial-load.circ as structural Verilog: 1 circuit, main circuit partial_load
module partial_load (
  input  [31:0] Instruction,
  input  [31:0] MemAddress,
  input  [31:0] DataFromMem,
  output [31:0] DataToReg
);

  wire and_1_out, and_2_out, and_3_out, and_4_out, and_5_out, and_6_out, and_7_out, and_8_out,
       comparator_1_eq, comparator_2_eq, comparator_3_eq, comparator_4_eq, decoder_1_out0, decoder_1_out1,
       decoder_1_out2, decoder_1_out3;
  wire [1:0] bit_extender_1_out;
  wire [2:0] priority_encoder_1_out;
  wire [31:0] bit_extender_2_out, bit_extender_3_out, bit_extender_4_out, bit_extender_5_out,
       bit_extender_6_out, bit_extender_7_out, bit_extender_8_out;

  Bit_Extender #(.in_width(32), .out_width(2), .\type ("zero")) bit_extender_1 (
    .in(MemAddress), .out(bit_extender_1_out));
  Decoder #(.enable("false"), .select(2)) decoder_1 (
    .out0(decoder_1_out0), .out1(decoder_1_out1), .out2(decoder_1_out2), .out3(decoder_1_out3),
    .sel(bit_extender_1_out));
  assign bit_extender_2_out = {{16{DataFromMem[15]}}, DataFromMem[15:0]};  // Bit_Extender bit_extender_2
  assign bit_extender_3_out = {{16{DataFromMem[23]}}, DataFromMem[23:8]};  // Bit_Extender bit_extender_3
  assign bit_extender_4_out = {{16{DataFromMem[31]}}, DataFromMem[31:16]};  // Bit_Extender bit_extender_4
  Comparator #(.width(7)) comparator_1 (.a(7'b0000011), .b(Instruction[6:0]), .eq(comparator_1_eq));  // open: gt, lt
  Comparator #(.width(3)) comparator_2 (.a(3'b000), .b(Instruction[14:12]), .eq(comparator_2_eq));  // open: gt, lt
  Comparator #(.width(3)) comparator_3 (.a(3'b001), .b(Instruction[14:12]), .eq(comparator_3_eq));  // open: gt, lt
  Comparator #(.width(3)) comparator_4 (.a(3'b010), .b(Instruction[14:12]), .eq(comparator_4_eq));  // open: gt, lt
  assign bit_extender_5_out = {{24{DataFromMem[7]}}, DataFromMem[7:0]};  // Bit_Extender bit_extender_5
  assign bit_extender_6_out = {{24{DataFromMem[15]}}, DataFromMem[15:8]};  // Bit_Extender bit_extender_6
  assign bit_extender_7_out = {{24{DataFromMem[23]}}, DataFromMem[23:16]};  // Bit_Extender bit_extender_7
  assign bit_extender_8_out = {{24{DataFromMem[31]}}, DataFromMem[31:24]};  // Bit_Extender bit_extender_8
  and and_1 (and_1_out, comparator_1_eq, comparator_2_eq, decoder_1_out0);
  and and_2 (and_2_out, comparator_1_eq, comparator_2_eq, decoder_1_out1);
  and and_3 (and_3_out, comparator_1_eq, comparator_2_eq, decoder_1_out2);
  and and_4 (and_4_out, comparator_1_eq, comparator_2_eq, decoder_1_out3);
  and and_5 (and_5_out, comparator_1_eq, comparator_3_eq, decoder_1_out0);
  and and_6 (and_6_out, comparator_1_eq, comparator_3_eq, decoder_1_out1);
  and and_7 (and_7_out, comparator_1_eq, comparator_3_eq, decoder_1_out2);
  and and_8 (and_8_out, comparator_1_eq, comparator_4_eq, decoder_1_out0);
  Multiplexer #(.select(3), .width(32)) multiplexer_1 (
    .in0(bit_extender_5_out), .in1(bit_extender_6_out), .in2(bit_extender_7_out), .in3(bit_extender_8_out),
    .in4(bit_extender_2_out), .in5(bit_extender_3_out), .in6(bit_extender_4_out), .in7(DataFromMem),
    .out(DataToReg), .sel(priority_encoder_1_out));
  Priority_Encoder priority_encoder_1 (
    .in0(and_1_out), .in1(and_2_out), .in2(and_3_out), .in3(and_4_out), .in4(and_5_out), .in5(and_6_out),
    .in6(and_7_out), .in7(and_8_out), .out(priority_encoder_1_out));  // open: en_in, gs, en_out

  // Notes on the sheet:
  //   INPUTS to your circuit
  //   DON'T CHANGE THE LOCATIONS OF THE INPUTS AND OUTPUTS!
  //   OUTPUT from your circuit
endmodule
