// Logisim project partial-store.circ as structural Verilog: 1 circuit, main circuit partial_store
module partial_store (
  input  [31:0] Instruction,
  input  [31:0] MemAddress,
  input  [31:0] DataFromReg,
  input  MemWEn,
  output [3:0] MemWriteMask,
  output [31:0] DataToMem
);

  wire and_1_out, and_2_out, and_3_out, and_4_out, and_5_out, and_6_out, and_7_out, comparator_1_eq,
       comparator_2_eq, comparator_3_eq, comparator_4_eq, decoder_1_out0, decoder_1_out1, decoder_1_out2,
       decoder_1_out3;
  wire [1:0] bit_extender_1_out;
  wire [2:0] priority_encoder_1_out;
  wire [3:0] multiplexer_1_out;
  wire [7:0] bit_extender_2_out;
  wire [15:0] bit_extender_3_out;
  wire [31:0] bit_extender_4_out, bit_extender_5_out;

  Decoder #(.enable("false"), .select(2)) decoder_1 (
    .out0(decoder_1_out0), .out1(decoder_1_out1), .out2(decoder_1_out2), .out3(decoder_1_out3),
    .sel(bit_extender_1_out));
  Bit_Extender #(.in_width(32), .out_width(2), .\type ("zero")) bit_extender_1 (
    .in(MemAddress), .out(bit_extender_1_out));
  Comparator #(.width(7)) comparator_1 (.a(7'b0100011), .b(Instruction[6:0]), .eq(comparator_1_eq));  // open: gt, lt
  Comparator #(.width(3)) comparator_2 (.a(3'b000), .b(Instruction[14:12]), .eq(comparator_2_eq));  // open: gt, lt
  Comparator #(.width(3)) comparator_3 (.a(3'b001), .b(Instruction[14:12]), .eq(comparator_3_eq));  // open: gt, lt
  Comparator #(.width(3)) comparator_4 (.a(3'b010), .b(Instruction[14:12]), .eq(comparator_4_eq));  // open: gt, lt
  Multiplexer #(.select(3), .width(4)) multiplexer_1 (
    .in0(4'b0001), .in1(4'b0010), .in2(4'b0100), .in3(4'b1000), .in4(4'b0011), .in5(4'b1100), .in6(4'b1111),
    .out(multiplexer_1_out), .sel(priority_encoder_1_out));  // open: in7
  and and_1 (and_1_out, comparator_1_eq, comparator_2_eq, decoder_1_out0);
  and and_2 (and_2_out, comparator_1_eq, comparator_2_eq, decoder_1_out1);
  and and_3 (and_3_out, comparator_1_eq, comparator_2_eq, decoder_1_out2);
  and and_4 (and_4_out, comparator_1_eq, comparator_2_eq, decoder_1_out3);
  and and_5 (and_5_out, comparator_1_eq, comparator_3_eq, decoder_1_out0);
  and and_6 (and_6_out, comparator_1_eq, comparator_3_eq, decoder_1_out2);
  and and_7 (and_7_out, comparator_1_eq, comparator_4_eq, decoder_1_out0);
  Bit_Extender #(.in_width(32), .out_width(8)) bit_extender_2 (.in(DataFromReg), .out(bit_extender_2_out));
  Bit_Extender #(.in_width(32)) bit_extender_3 (.in(DataFromReg), .out(bit_extender_3_out));
  Multiplexer #(.width(4)) multiplexer_2 (.in0(4'b0000), .in1(multiplexer_1_out), .out(MemWriteMask), .sel(MemWEn));
  assign bit_extender_4_out = {{24{1'b0}}, bit_extender_2_out};  // Bit_Extender bit_extender_4
  assign bit_extender_5_out = {{16{1'b0}}, bit_extender_3_out};  // Bit_Extender bit_extender_5
  Priority_Encoder priority_encoder_1 (
    .in0(and_1_out), .in1(and_2_out), .in2(and_3_out), .in3(and_4_out), .in4(and_5_out), .in5(and_6_out),
    .in6(and_7_out), .out(priority_encoder_1_out));  // open: in7, en_in, gs, en_out
  Multiplexer #(.select(3), .width(32)) multiplexer_3 (
    .in0(bit_extender_4_out), .in1({{16{1'b0}}, bit_extender_2_out, {8{1'b0}}}),
    .in2({{8{1'b0}}, bit_extender_2_out, {16{1'b0}}}), .in3({bit_extender_2_out, {24{1'b0}}}),
    .in4(bit_extender_5_out), .in5({bit_extender_3_out, {16{1'b0}}}), .in6(DataFromReg), .out(DataToMem));  // open: in7, sel

  // Notes on the sheet:
  //   INPUTS to your circuit
  //   DON'T CHANGE THE LOCATIONS OF THE INPUTS AND OUTPUTS!
  //   OUTPUT from your circuit
endmodule
