// Logisim project regfile.circ as structural Verilog: 1 circuit, main circuit regfile
module regfile (
  input  [4:0] ReadIndex1,
  input  [4:0] ReadIndex2,
  input  [4:0] WriteIndex,
  input  [31:0] WriteData,
  input  RegWEn,
  input  clk,
  output [31:0] ra,
  output [31:0] sp,
  output [31:0] t0,
  output [31:0] t1,
  output [31:0] t2,
  output [31:0] s0,
  output [31:0] s1,
  output [31:0] a0,
  output [31:0] ReadData1,
  output [31:0] ReadData2
);

  wire x1, x2, x3, x4, x5, x6, x7, x8, x9, x10, x11, x12, x13, x14, x15, x16, x17, x18, x19, x20, x21, x22,
       x23, x24, x25, x26, x27, x28, x29, x30, x31;
  wire [31:0] Outx3, Outx4, Outx11, Outx12, Outx13, Outx14, Outx15, Outx16, Outx17, Outx18, Outx19, Outx20,
       Outx21, Outx22, Outx23, Outx24, Outx25, Outx26, Outx27, Outx28, Outx29, Outx30, Outx31;

  Decoder #(.select(5)) decoder_1 (
    .out1(x1), .out2(x2), .out3(x3), .out4(x4), .out5(x5), .out6(x6), .out7(x7), .out8(x8), .out9(x9),
    .out10(x10), .out11(x11), .out12(x12), .out13(x13), .out14(x14), .out15(x15), .out16(x16), .out17(x17),
    .out18(x18), .out19(x19), .out20(x20), .out21(x21), .out22(x22), .out23(x23), .out24(x24), .out25(x25),
    .out26(x26), .out27(x27), .out28(x28), .out29(x29), .out30(x30), .out31(x31), .sel(WriteIndex),
    .en(RegWEn));  // open: out0
  Register #(.width(32)) register_1 (.D(WriteData), .en(x1), .clk(clk), .Q(ra));  // open: clr
  Register #(.width(32)) register_2 (.D(WriteData), .en(x2), .clk(clk), .Q(sp));  // open: clr
  Register #(.width(32)) register_3 (.D(WriteData), .en(x3), .clk(clk), .Q(Outx3));  // open: clr
  Register #(.width(32)) register_4 (.D(WriteData), .en(x4), .clk(clk), .Q(Outx4));  // open: clr
  Register #(.width(32)) register_5 (.D(WriteData), .en(x5), .clk(clk), .Q(t0));  // open: clr
  Register #(.width(32)) register_6 (.D(WriteData), .en(x6), .clk(clk), .Q(t1));  // open: clr
  Register #(.width(32)) register_7 (.D(WriteData), .en(x7), .clk(clk), .Q(t2));  // open: clr
  Register #(.width(32)) register_8 (.D(WriteData), .en(x8), .clk(clk), .Q(s0));  // open: clr
  Register #(.width(32)) register_9 (.D(WriteData), .en(x9), .clk(clk), .Q(s1));  // open: clr
  Register #(.width(32)) register_10 (.D(WriteData), .en(x10), .clk(clk), .Q(a0));  // open: clr
  Register #(.width(32)) register_11 (.D(WriteData), .en(x11), .clk(clk), .Q(Outx11));  // open: clr
  Register #(.width(32)) register_12 (.D(WriteData), .en(x12), .clk(clk), .Q(Outx12));  // open: clr
  Register #(.width(32)) register_13 (.D(WriteData), .en(x13), .clk(clk), .Q(Outx13));  // open: clr
  Register #(.width(32)) register_14 (.D(WriteData), .en(x14), .clk(clk), .Q(Outx14));  // open: clr
  Register #(.width(32)) register_15 (.D(WriteData), .en(x15), .clk(clk), .Q(Outx15));  // open: clr
  Register #(.width(32)) register_16 (.D(WriteData), .en(x16), .clk(clk), .Q(Outx16));  // open: clr
  Register #(.width(32)) register_17 (.D(WriteData), .en(x17), .clk(clk), .Q(Outx17));  // open: clr
  Register #(.width(32)) register_18 (.D(WriteData), .en(x18), .clk(clk), .Q(Outx18));  // open: clr
  Register #(.width(32)) register_19 (.D(WriteData), .en(x19), .clk(clk), .Q(Outx19));  // open: clr
  Register #(.width(32)) register_20 (.D(WriteData), .en(x20), .clk(clk), .Q(Outx20));  // open: clr
  Register #(.width(32)) register_21 (.D(WriteData), .en(x21), .clk(clk), .Q(Outx21));  // open: clr
  Register #(.width(32)) register_22 (.D(WriteData), .en(x22), .clk(clk), .Q(Outx22));  // open: clr
  Register #(.width(32)) register_23 (.D(WriteData), .en(x23), .clk(clk), .Q(Outx23));  // open: clr
  Register #(.width(32)) register_24 (.D(WriteData), .en(x24), .clk(clk), .Q(Outx24));  // open: clr
  Register #(.width(32)) register_25 (.D(WriteData), .en(x25), .clk(clk), .Q(Outx25));  // open: clr
  Register #(.width(32)) register_26 (.D(WriteData), .en(x26), .clk(clk), .Q(Outx26));  // open: clr
  Register #(.width(32)) register_27 (.D(WriteData), .en(x27), .clk(clk), .Q(Outx27));  // open: clr
  Register #(.width(32)) register_28 (.D(WriteData), .en(x28), .clk(clk), .Q(Outx28));  // open: clr
  Register #(.width(32)) register_29 (.D(WriteData), .en(x29), .clk(clk), .Q(Outx29));  // open: clr
  Register #(.width(32)) register_30 (.D(WriteData), .en(x30), .clk(clk), .Q(Outx30));  // open: clr
  Register #(.width(32)) register_31 (.D(WriteData), .en(x31), .clk(clk), .Q(Outx31));  // open: clr
  Multiplexer #(.select(5), .width(32)) multiplexer_1 (
    .in0({32{1'b0}}), .in1(ra), .in2(sp), .in3(Outx3), .in4(Outx4), .in5(t0), .in6(t1), .in7(t2), .in8(s0),
    .in9(s1), .in10(a0), .in11(Outx11), .in12(Outx12), .in13(Outx13), .in14(Outx14), .in15(Outx15),
    .in16(Outx16), .in17(Outx17), .in18(Outx18), .in19(Outx19), .in20(Outx20), .in21(Outx21), .in22(Outx22),
    .in23(Outx23), .in24(Outx24), .in25(Outx25), .in26(Outx26), .in27(Outx27), .in28(Outx28), .in29(Outx29),
    .in30(Outx30), .in31(Outx31), .out(ReadData2), .sel(ReadIndex2));
  Multiplexer #(.select(5), .width(32)) multiplexer_2 (
    .in0({32{1'b0}}), .in1(ra), .in2(sp), .in3(Outx3), .in4(Outx4), .in5(t0), .in6(t1), .in7(t2), .in8(s0),
    .in9(s1), .in10(a0), .in11(Outx11), .in12(Outx12), .in13(Outx13), .in14(Outx14), .in15(Outx15),
    .in16(Outx16), .in17(Outx17), .in18(Outx18), .in19(Outx19), .in20(Outx20), .in21(Outx21), .in22(Outx22),
    .in23(Outx23), .in24(Outx24), .in25(Outx25), .in26(Outx26), .in27(Outx27), .in28(Outx28), .in29(Outx29),
    .in30(Outx30), .in31(Outx31), .out(ReadData1), .sel(ReadIndex1));

  // Other names for the same wires on the sheet: Outx1[31:0] = ra; Outx2[31:0] = sp; Outx5[31:0] = t0;
  //   Outx6[31:0] = t1; Outx7[31:0] = t2; Outx8[31:0] = s0; Outx9[31:0] = s1; Outx10[31:0] = a0

  // Notes on the sheet:
  //   INPUTS to your circuit
  //   DON'T CHANGE THE LOCATIONS OF THE INPUTS AND OUTPUTS!
  //   These are DEBUG/TEST outputs from your circuit.
  //   OUTPUTS from your circuit
endmodule
